// Digital circuit Main.dig as structural Verilog
module Main (
  input  Clock
);

  wire [1:0] Stage_1_fetch_suppress, Stage_2_spsidi, undriven_4;
  wire [2:0] Control_const, Stage_2_addr;
  wire [3:0] alu_1_p7, Control_gpr_a, Control_gpr_b, Control_gpr_c, Control_gpr_d, Control_mem, undriven_3;
  wire [5:0] Control_dev_load;
  wire [6:0] Control_dev_assert, Control_di, Control_pcra0, Control_pcra1, Control_si, Control_sp, Reset_out,
       undriven_2;
  wire [7:0] A_i, A_lhs, A_rhs, B_i, C_i, Constant_i, Control_xfer_2, D_i, Fetch_pipeout, memory_1_mem,
       Stage_1_pipeout, Stage_2_main, transfer_register_1_main;
  wire [15:0] DI_i, PCRA0_addr, PCRA0_i, PCRA1_i, SI_i, SP_i, transfer_register_1_i, undriven;

  Address_Register PCRA0 (.xfer(undriven), .ADDR(PCRA0_addr), .Control(Control_pcra0), .I(PCRA0_i));
  Address_Register PCRA1 (.xfer(undriven), .ADDR(PCRA0_addr), .Control(Control_pcra1), .I(PCRA1_i));
  Address_Register SP (.xfer(undriven), .ADDR(PCRA0_addr), .Control(Control_sp), .I(SP_i));
  Address_Register SI (.xfer(undriven), .ADDR(PCRA0_addr), .Control(Control_si), .I(SI_i));
  Address_Register DI (.xfer(undriven), .ADDR(PCRA0_addr), .Control(Control_di), .I(DI_i));
  Transfer_Register transfer_register_1 (
    .MAIN(transfer_register_1_main), .XFER(undriven), .ADDR(PCRA0_addr), .C(Control_xfer_2),
    .I(transfer_register_1_i));
  Memory memory_1 (.ADDR(PCRA0_addr), .Control(Control_mem), .MEM(memory_1_mem));
  // Probe on PCRA0_i
  // Probe on PCRA1_i
  // Probe on SP_i
  // Probe on SI_i
  // Probe on DI_i
  // Probe ADDR on PCRA0_addr
  // Probe XFER on undriven
  // Probe MEM on memory_1_mem
  Bus_Control Control (
    .Dev_Load(Control_dev_load), .Main(Stage_2_main), .Xfer(undriven_2), .Clock(Clock), .Reset(Reset_out[6]),
    .Inc({Stage_2_spsidi, undriven_4}), .ALU_Assert(undriven_3), .Addr_Assert(Stage_2_addr),
    .Dev_Assert(Control_dev_assert), .PCRA0(Control_pcra0), .PCRA1(Control_pcra1), .SP(Control_sp),
    .SI(Control_si), .DI(Control_di), .GPR_A(Control_gpr_a), .GPR_B(Control_gpr_b), .GPR_C(Control_gpr_c),
    .GPR_D(Control_gpr_d), .Const(Control_const), .XFER_2(Control_xfer_2), .Mem(Control_mem));
  // Probe on transfer_register_1_i
  GPR A (.RHS(A_rhs), .LHS(A_lhs), .MAIN(transfer_register_1_main), .Control(Control_gpr_a), .I(A_i));
  GPR B (.RHS(A_rhs), .LHS(A_lhs), .MAIN(transfer_register_1_main), .Control(Control_gpr_b), .I(B_i));
  GPR C (.RHS(A_rhs), .LHS(A_lhs), .MAIN(transfer_register_1_main), .Control(Control_gpr_c), .I(C_i));
  GPR D (.RHS(A_rhs), .LHS(A_lhs), .MAIN(transfer_register_1_main), .Control(Control_gpr_d), .I(D_i));
  Constant_Register Constant (
    .Control(Control_const), .MEM(memory_1_mem), .MAIN(transfer_register_1_main), .I(Constant_i));
  Memory_Bridge memory_bridge_1 (.MAIN(transfer_register_1_main), .MEM(memory_1_mem), .Control(Control_mem));
  // Probe on A_i
  // Probe on B_i
  // Probe on C_i
  // Probe on D_i
  // Probe on Constant_i
  // Probe RHS on A_rhs
  // Probe LHS on A_lhs
  // Probe MAIN on transfer_register_1_main
  // ALU alu_1: pin names not known; wires that end beside it: Control_dev_assert[0], A_rhs, A_lhs, transfer_register_1_main, Reset_out[4:0], Clock, alu_1_p7
  Stage_2 Stage_2 (
    .Flags(Reset_out), .Clock(Clock), .PipeIn(Stage_1_pipeout), .Main(Stage_2_main), .SPSIDI(Stage_2_spsidi),
    .Addr(Stage_2_addr), .Bus_Request(Stage_1_fetch_suppress[1]), .PCRA_Flip(Reset_out[5]));  // open: Break
  Stage_1 Stage_1 (
    .ALU_Bus(undriven_3), .ALU_Ops(alu_1_p7), .Xfer(undriven_2), .Fetch_suppress(Stage_1_fetch_suppress[0]),
    .Control(Stage_1_fetch_suppress), .PipeOut(Stage_1_pipeout), .Flags(Reset_out), .Clock(Clock),
    .PipeIn(Fetch_pipeout));
  Fetch Fetch (
    .MEM(memory_1_mem), .Flags(Reset_out), .Clock(Clock), .PCRA(undriven_4),
    .Control(Stage_1_fetch_suppress), .PipeOut(Fetch_pipeout));
  Button #(.activeLow("true")) Reset (.out(Reset_out[6]));
  Terminal terminal_1 (.D(transfer_register_1_main), .C(Clock), .Load(Control_dev_load[0]));
  // Probe Stage1 on Fetch_pipeout
  // Probe Inc on {Stage_2_spsidi, undriven_4}
  // Probe Addr on Stage_2_addr
  // Probe ALU Ops on alu_1_p7
  // Probe ALU Bus on undriven_3
  // Probe Xfer on undriven_2
  // Probe Main on Stage_2_main

  // Notes on the sheet:
  //   Clock: Hz: 10
  //   contents of ROM (hex, n*v repeats v):
  //   0,5,1,6,0,29,5,2f,6,0,27,5,14,6,0,5c,0,2a,5f,60,2a,72,76,77,0,5,22,6,0,29,5,29,6, 0,5b,fc,5f,
  //   65,39,5f,71,7d,7c,78,29,5e,0,48,65,6c,6c,6f,20,57,6f,72,6c,64,21,5c,6e
endmodule
